# Fritzing sketch pcb_cubo (saved by Fritzing 0.9.3b)
circuit board: 8.46667cm x 5.64444cm
breadboards: 1

parts:
  R1 = Resistor [tolerance=±5% resistance=27 package="0402 [SMD]"]
  LED1 = LED - 3mm [color="Red (633nm)" package="3 mm [THT]"]
  U1 = attiny85 [package=dip]
  Q1 = NPN-Transistor [part_number=BC337 package="TO92 [THT]"]
  VCC1 = 4 x AAA Battery Mount

nets:
  N1: R1.Pin_0, R1.Pin_1, LED1.cathode, U1.Pin_8, VCC1.+
  N2: LED1.anode, Q1.E
  N3: U1.Pin_4, Q1.C, VCC1.-
  N4: U1.Pin_6, Q1.B

notes:
  VCC IN 5V
  Transistor BC337
  Resistenza 27 OHM
